// Logisim project Project Logic (DIGITAL CLOCK) .circ as structural Verilog: 5 circuits, main circuit main
module Ones_mins (
  input  A3,
  input  A2,
  input  A1,
  input  A0,
  output A,
  output B,
  output C,
  output D,
  output E,
  output F,
  output G
);

  wire and_1_out, and_2_out, and_3_out, and_4_out, and_5_out, and_6_out, and_7_out, and_8_out, and_9_out,
       and_10_out, and_11_out, and_12_out, and_13_out, and_14_out, and_15_out, and_16_out, and_17_out,
       not_1_out, not_2_out, not_3_out, not_4_out, not_5_out, not_6_out, not_7_out, not_8_out, not_9_out,
       not_10_out, not_11_out, not_12_out, not_13_out, not_14_out, not_15_out, not_16_out, not_17_out,
       not_18_out, not_19_out, not_20_out, not_21_out, or_1_out, or_2_out, or_3_out, or_4_out, or_7_out,
       or_8_out, or_9_out, or_10_out, or_13_out, or_14_out;

  not not_1 (not_1_out, A2);
  and and_1 (and_1_out, not_1_out, not_2_out);
  not not_2 (not_2_out, A0);
  and and_2 (and_2_out, A2, A0);
  not not_3 (not_3_out, A2);
  not not_4 (not_4_out, A1);
  and and_3 (and_3_out, not_4_out, not_5_out);
  not not_5 (not_5_out, A0);
  not not_6 (not_6_out, A1);
  or or_1 (or_1_out, not_6_out, A0);
  not not_7 (not_7_out, A2);
  not not_8 (not_8_out, A0);
  not not_9 (not_9_out, A2);
  not not_10 (not_10_out, A0);
  and and_4 (and_4_out, A2, not_11_out);
  not not_11 (not_11_out, A1);
  not not_12 (not_12_out, A2);
  and and_5 (and_5_out, not_12_out, not_13_out);
  not not_13 (not_13_out, A0);
  and and_6 (and_6_out, A1, not_14_out);
  not not_14 (not_14_out, A0);
  not not_15 (not_15_out, A1);
  and and_7 (and_7_out, not_15_out, not_16_out);
  not not_16 (not_16_out, A0);
  and and_8 (and_8_out, A2, not_17_out);
  not not_17 (not_17_out, A1);
  and and_9 (and_9_out, A2, not_18_out);
  not not_18 (not_18_out, A0);
  not not_19 (not_19_out, A2);
  and and_10 (and_10_out, not_19_out, A1);
  and and_11 (and_11_out, A2, not_20_out);
  not not_20 (not_20_out, A1);
  and and_12 (and_12_out, A2, not_21_out);
  not not_21 (not_21_out, A0);
  or or_2 (or_2_out, and_1_out, A1);
  or or_3 (or_3_out, and_2_out, A3);
  or or_4 (or_4_out, not_3_out, and_3_out);
  and and_13 (and_13_out, A1, A0);
  or or_5 (C, or_1_out, A2);
  and and_14 (and_14_out, not_7_out, not_8_out);
  and and_15 (and_15_out, not_9_out, A1);
  and and_16 (and_16_out, A1, not_10_out);
  and and_17 (and_17_out, and_4_out, A0);
  or or_6 (E, and_5_out, and_6_out);
  or or_7 (or_7_out, and_7_out, and_8_out);
  or or_8 (or_8_out, and_9_out, A3);
  or or_9 (or_9_out, and_10_out, and_11_out);
  or or_10 (or_10_out, and_12_out, A3);
  or or_11 (A, or_2_out, or_3_out);
  or or_12 (B, or_4_out, and_13_out);
  or or_13 (or_13_out, and_14_out, and_15_out);
  or or_14 (or_14_out, and_16_out, and_17_out);
  or or_15 (F, or_7_out, or_8_out);
  or or_16 (G, or_9_out, or_10_out);
  or or_17 (D, or_13_out, or_14_out);
endmodule

module Tens_Seconds (
  input  Q2,
  input  Q1,
  input  Q0,
  output A,
  output B,
  output C,
  output D,
  output E,
  output F,
  output G
);

  wire and_1_out, and_2_out, and_3_out, and_4_out, and_5_out, and_6_out, and_7_out, not_1_out, not_2_out,
       not_3_out, not_4_out, not_5_out, not_6_out, not_7_out, not_8_out, not_9_out, not_10_out, not_11_out,
       or_2_out, or_3_out, or_4_out, or_7_out;

  not not_1 (not_1_out, Q2);
  not not_2 (not_2_out, Q0);
  not not_3 (not_3_out, Q2);
  not not_4 (not_4_out, Q0);
  not not_5 (not_5_out, Q1);
  not not_6 (not_6_out, Q2);
  not not_7 (not_7_out, Q0);
  not not_8 (not_8_out, Q2);
  not not_9 (not_9_out, Q0);
  not not_10 (not_10_out, Q1);
  not not_11 (not_11_out, Q0);
  or or_1 (G, Q1, Q2);
  and and_1 (and_1_out, not_1_out, not_2_out);
  or or_2 (or_2_out, not_3_out, not_4_out);
  or or_3 (or_3_out, not_5_out, Q0);
  and and_2 (and_2_out, not_6_out, not_7_out);
  and and_3 (and_3_out, not_8_out, not_9_out);
  and and_4 (and_4_out, Q2, Q1);
  and and_5 (and_5_out, not_10_out, not_11_out);
  or or_4 (or_4_out, and_1_out, Q1);
  and and_6 (and_6_out, Q2, Q0);
  or or_5 (B, or_2_out, Q1);
  or or_6 (C, or_3_out, Q2);
  or or_7 (or_7_out, and_2_out, Q1);
  and and_7 (and_7_out, Q2, Q0);
  or or_8 (E, and_3_out, and_4_out);
  or or_9 (F, and_5_out, Q2);
  or or_10 (A, or_4_out, and_6_out);
  or or_11 (D, or_7_out, and_7_out);
endmodule

module main (
);

  wire _59_secs___9_mins_out, A0_2_q, A0_and_A3_ones_minites_out, A0_and_A3_out, A0_q, A1_2_q, A1_q, A2_2_q,
       A2_q, A3_2_q, A3_q, and_1_out, and_2_out, and_3_out, and_4_out, and_5_out, and_6_out, and_7_out,
       and_8_out, and_9_out, and_10_out, and_11_out, and_12_out, and_13_out, and_14_out, and_15_out,
       and_16_out, and_17_out, and_18_out, and_19_out, and_20_out, clock_1_out,
       H0_and_H3_and_T0_hours_ones_out, H0_q, H1_q, H2_q, H3_and_H1__10_out, H3_q, H_tens_q, H_tens_qn,
       hours_ones_1_a, hours_ones_1_b, hours_ones_1_c, hours_ones_1_d, hours_ones_1_e, hours_ones_1_f,
       hours_ones_1_g, ones_mins_1_a, ones_mins_1_b, ones_mins_1_c, ones_mins_1_d, ones_mins_1_e,
       ones_mins_1_f, ones_mins_1_g, ones_mins_2_a, ones_mins_2_b, ones_mins_2_c, ones_mins_2_d,
       ones_mins_2_e, ones_mins_2_f, ones_mins_2_g, or_1_out, Q0_and_Q2__min_tens_out, Q0_and_Q2_out, S0_2_q,
       S0_q, S1_2_q, S1_q, S2_2_q, S2_q, T0_mins_ones_and_output_tens_mins_out, t_ff_1_qn, tens_seconds_1_a,
       tens_seconds_1_b, tens_seconds_1_c, tens_seconds_1_d, tens_seconds_1_e, tens_seconds_1_f,
       tens_seconds_1_g, tens_seconds_2_a, tens_seconds_2_b, tens_seconds_2_c, tens_seconds_2_d,
       tens_seconds_2_e, tens_seconds_2_f, tens_seconds_2_g;

  Clock clock_1 (.out(clock_1_out));
  and and_1 (and_1_out, A0_and_A3_out, S0_q);
  and and_2 (and_2_out, S1_q, and_1_out);
  T_Flip_Flop S0 (.clk(clock_1_out), .T(A0_and_A3_out), .Q(S0_q), .reset(and_3_out));  // open: Qn, preset, en
  T_Flip_Flop S1 (.clk(clock_1_out), .T(and_1_out), .Q(S1_q), .reset(and_3_out));  // open: Qn, preset, en
  T_Flip_Flop S2 (.clk(clock_1_out), .T(and_2_out), .Q(S2_q), .reset(and_3_out));  // open: Qn, preset, en
  and and_3 (and_3_out, S2_q, S1_q);
  Tens_Seconds tens_seconds_1 (
    .Q2(S2_q), .Q1(S1_q), .Q0(S0_q), .A(tens_seconds_1_a), .B(tens_seconds_1_b), .C(tens_seconds_1_c),
    .D(tens_seconds_1_d), .E(tens_seconds_1_e), .F(tens_seconds_1_f), .G(tens_seconds_1_g));
  _7_Segment_Display u_7_segment_display_1 (
    .g(tens_seconds_1_g), .f(tens_seconds_1_f), .a(tens_seconds_1_a), .b(tens_seconds_1_b),
    .e(tens_seconds_1_e), .d(tens_seconds_1_d), .c(tens_seconds_1_c));  // open: dp
  _7_Segment_Display u_7_segment_display_2 (
    .g(ones_mins_1_g), .f(ones_mins_1_f), .a(ones_mins_1_a), .b(ones_mins_1_b), .e(ones_mins_1_e),
    .d(ones_mins_1_d), .c(ones_mins_1_c));  // open: dp
  _7_Segment_Display u_7_segment_display_3 (
    .g(tens_seconds_2_g), .f(tens_seconds_2_f), .a(tens_seconds_2_a), .b(tens_seconds_2_b),
    .e(tens_seconds_2_e), .d(tens_seconds_2_d), .c(tens_seconds_2_c));  // open: dp
  _7_Segment_Display u_7_segment_display_4 (
    .g(1'b1), .f(1'b1), .a(1'b1), .b(1'b1), .e(1'b1), .c(t_ff_1_qn));  // open: d, dp
  and A0_and_A3 (A0_and_A3_out, A3_q, A0_q);
  Ones_mins ones_mins_1 (
    .A3(A3_q), .A2(A2_q), .A1(A1_q), .A0(A0_q), .A(ones_mins_1_a), .B(ones_mins_1_b), .C(ones_mins_1_c),
    .D(ones_mins_1_d), .E(ones_mins_1_e), .F(ones_mins_1_f), .G(ones_mins_1_g));
  _7_Segment_Display u_7_segment_display_5 (
    .g(ones_mins_2_g), .f(ones_mins_2_f), .a(ones_mins_2_a), .b(ones_mins_2_b), .e(ones_mins_2_e),
    .d(ones_mins_2_d), .c(ones_mins_2_c), .dp(ones_mins_2_c));
  DotMatrix #(.matrixcols(7)) dotmatrix_1 (
    .col0({7{1'b1}}), .col1(7'b1000000), .col2(7'b0100000), .col3(7'b0010000), .col4(7'b0100000),
    .col5(7'b1000000), .col6({7{1'b1}}));
  and Q0_and_Q2 (Q0_and_Q2_out, S0_q, S2_q);
  _7_Segment_Display u_7_segment_display_6 (
    .f(H_tens_qn), .a(H_tens_qn), .b(1'b1), .e(H_tens_qn), .d(H_tens_qn), .c(1'b1));  // open: g, dp
  _7_Segment_Display u_7_segment_display_7 (
    .g(hours_ones_1_g), .f(hours_ones_1_f), .a(hours_ones_1_a), .b(hours_ones_1_b), .e(hours_ones_1_e),
    .d(hours_ones_1_d), .c(hours_ones_1_c));  // open: dp
  and and_4 (and_4_out, A0_q, A1_q);
  and and_5 (and_5_out, and_4_out, A2_q);
  T_Flip_Flop A0 (.clk(clock_1_out), .T(1'b1), .Q(A0_q), .reset(and_6_out));  // open: Qn, preset, en
  T_Flip_Flop A1 (.clk(clock_1_out), .T(A0_q), .Q(A1_q), .reset(and_6_out));  // open: Qn, preset, en
  T_Flip_Flop A2 (.clk(clock_1_out), .T(and_4_out), .Q(A2_q), .reset(and_6_out));  // open: Qn, preset, en
  T_Flip_Flop A3 (.clk(clock_1_out), .T(and_5_out), .Q(A3_q), .reset(and_6_out));  // open: Qn, preset, en
  and and_6 (and_6_out, A1_q, A3_q);
  and _59_secs___9_mins (_59_secs___9_mins_out, and_10_out, A0_and_A3_ones_minites_out);
  and and_7 (and_7_out, _59_secs___9_mins_out, S0_2_q);
  and and_8 (and_8_out, S1_2_q, and_7_out);
  T_Flip_Flop S0_2 (
    .clk(clock_1_out), .T(_59_secs___9_mins_out), .Q(S0_2_q), .reset(and_9_out));  // open: Qn, preset, en
  T_Flip_Flop S1_2 (.clk(clock_1_out), .T(and_7_out), .Q(S1_2_q), .reset(and_9_out));  // open: Qn, preset, en
  T_Flip_Flop S2_2 (.clk(clock_1_out), .T(and_8_out), .Q(S2_2_q), .reset(and_9_out));  // open: Qn, preset, en
  and and_9 (and_9_out, S2_2_q, S1_2_q);
  Tens_Seconds tens_seconds_2 (
    .Q2(S2_2_q), .Q1(S1_2_q), .Q0(S0_2_q), .A(tens_seconds_2_a), .B(tens_seconds_2_b), .C(tens_seconds_2_c),
    .D(tens_seconds_2_d), .E(tens_seconds_2_e), .F(tens_seconds_2_f), .G(tens_seconds_2_g));
  and A0_and_A3_ones_minites (A0_and_A3_ones_minites_out, A3_2_q, A0_2_q);
  and Q0_and_Q2__min_tens (Q0_and_Q2__min_tens_out, S0_2_q, S2_2_q);
  Ones_mins ones_mins_2 (
    .A3(A3_2_q), .A2(A2_2_q), .A1(A1_2_q), .A0(A0_2_q), .A(ones_mins_2_a), .B(ones_mins_2_b),
    .C(ones_mins_2_c), .D(ones_mins_2_d), .E(ones_mins_2_e), .F(ones_mins_2_f), .G(ones_mins_2_g));
  and and_10 (and_10_out, A0_and_A3_out, Q0_and_Q2_out);
  and and_11 (and_11_out, A0_2_q, and_10_out);
  and and_12 (and_12_out, and_11_out, A1_2_q);
  and and_13 (and_13_out, and_12_out, A2_2_q);
  T_Flip_Flop A0_2 (.clk(clock_1_out), .T(and_10_out), .Q(A0_2_q), .reset(and_14_out));  // open: Qn, preset, en
  T_Flip_Flop A1_2 (.clk(clock_1_out), .T(and_11_out), .Q(A1_2_q), .reset(and_14_out));  // open: Qn, preset, en
  T_Flip_Flop A2_2 (.clk(clock_1_out), .T(and_12_out), .Q(A2_2_q), .reset(and_14_out));  // open: Qn, preset, en
  T_Flip_Flop A3_2 (.clk(clock_1_out), .T(and_13_out), .Q(A3_2_q), .reset(and_14_out));  // open: Qn, preset, en
  and and_14 (and_14_out, A3_2_q, A1_2_q);
  and T0_mins_ones_and_output_tens_mins (T0_mins_ones_and_output_tens_mins_out, Q0_and_Q2__min_tens_out, _59_secs___9_mins_out);
  Hours_ones hours_ones_1 (
    .H3(H3_q), .H2(H2_q), .H1(H1_q), .H0(H0_q), .a(hours_ones_1_a), .b(hours_ones_1_b), .c(hours_ones_1_c),
    .d(hours_ones_1_d), .e(hours_ones_1_e), .f(hours_ones_1_f), .g(hours_ones_1_g));
  and and_15 (and_15_out, and_17_out, H2_q);
  and and_16 (and_16_out, H0_q, T0_mins_ones_and_output_tens_mins_out);
  and and_17 (and_17_out, H1_q, and_16_out);
  T_Flip_Flop H0 (
    .clk(clock_1_out), .T(T0_mins_ones_and_output_tens_mins_out), .Q(H0_q));  // open: Qn, preset, reset, en
  T_Flip_Flop H1 (.clk(clock_1_out), .T(and_16_out), .Q(H1_q), .reset(or_1_out));  // open: Qn, preset, en
  T_Flip_Flop H2 (.clk(clock_1_out), .T(and_17_out), .Q(H2_q), .reset(or_1_out));  // open: Qn, preset, en
  T_Flip_Flop H3 (.clk(clock_1_out), .T(and_15_out), .Q(H3_q), .reset(or_1_out));  // open: Qn, preset, en
  and H3_and_H1__10 (H3_and_H1__10_out, H3_q, H1_q);
  or or_1 (or_1_out, H3_and_H1__10_out, and_18_out);
  and and_18 (and_18_out, H0_q, H1_q, H_tens_q);
  and H0_and_H3_and_T0_hours_ones (H0_and_H3_and_T0_hours_ones_out, H0_q, H3_q, T0_mins_ones_and_output_tens_mins_out);
  T_Flip_Flop H_tens (
    .clk(clock_1_out), .T(H0_and_H3_and_T0_hours_ones_out), .Q(H_tens_q), .Qn(H_tens_qn), .reset(and_18_out));  // open: preset, en
  and and_19 (and_19_out, H0_q, H_tens_q);
  and and_20 (and_20_out, and_19_out, T0_mins_ones_and_output_tens_mins_out);
  T_Flip_Flop t_ff_1 (.clk(clock_1_out), .T(and_20_out), .Qn(t_ff_1_qn));  // open: Q, preset, reset, en
  T_Flip_Flop t_ff_2 ();  // open: clk, T, Q, Qn, preset, reset, en

  // Notes on the sheet:
  //   ٍ
  //   Seconds
  //   Minutes
  //   Hours
  //   A3
  //   A2
  //   D
  //   A1
  //   A0
  //   G
  //   A
  //   B
  //   C
  //   E
  //   F
  //   A3
  //   ِِ
  //   A1
  //   A0
  //   H0
  //   _
  //   Q (Hours Tens)
  //   H0
endmodule

module Hours_ones (
  input  H3,
  input  H2,
  input  H1,
  input  H0,
  output a,
  output b,
  output c,
  output d,
  output e,
  output f,
  output g
);

  wire and_1_out, and_2_out, and_3_out, and_4_out, and_5_out, and_6_out, and_7_out, and_8_out, and_9_out,
       and_10_out, and_11_out, and_12_out, and_13_out, and_14_out, and_15_out, and_16_out, and_17_out,
       not_1_out, not_2_out, not_3_out, not_4_out, not_5_out, not_6_out, not_7_out, not_8_out, not_9_out,
       not_10_out, not_11_out, not_12_out, not_13_out, not_14_out, not_15_out, not_16_out, not_17_out,
       not_18_out, not_19_out, not_20_out, not_21_out, or_1_out, or_2_out, or_3_out, or_4_out, or_7_out,
       or_8_out, or_9_out, or_10_out, or_13_out, or_14_out;

  not not_1 (not_1_out, H2);
  and and_1 (and_1_out, not_1_out, not_2_out);
  not not_2 (not_2_out, H0);
  and and_2 (and_2_out, H2, H0);
  not not_3 (not_3_out, H2);
  not not_4 (not_4_out, H1);
  and and_3 (and_3_out, not_4_out, not_5_out);
  not not_5 (not_5_out, H0);
  not not_6 (not_6_out, H1);
  or or_1 (or_1_out, not_6_out, H0);
  not not_7 (not_7_out, H2);
  not not_8 (not_8_out, H0);
  not not_9 (not_9_out, H2);
  not not_10 (not_10_out, H0);
  and and_4 (and_4_out, H2, not_11_out);
  not not_11 (not_11_out, H1);
  not not_12 (not_12_out, H2);
  and and_5 (and_5_out, not_12_out, not_13_out);
  not not_13 (not_13_out, H0);
  and and_6 (and_6_out, H1, not_14_out);
  not not_14 (not_14_out, H0);
  not not_15 (not_15_out, H1);
  and and_7 (and_7_out, not_15_out, not_16_out);
  not not_16 (not_16_out, H0);
  and and_8 (and_8_out, H2, not_17_out);
  not not_17 (not_17_out, H1);
  and and_9 (and_9_out, H2, not_18_out);
  not not_18 (not_18_out, H0);
  not not_19 (not_19_out, H2);
  and and_10 (and_10_out, not_19_out, H1);
  and and_11 (and_11_out, H2, not_20_out);
  not not_20 (not_20_out, H1);
  and and_12 (and_12_out, H2, not_21_out);
  not not_21 (not_21_out, H0);
  or or_2 (or_2_out, and_1_out, H1);
  or or_3 (or_3_out, and_2_out, H3);
  or or_4 (or_4_out, not_3_out, and_3_out);
  and and_13 (and_13_out, H1, H0);
  or or_5 (c, or_1_out, H2);
  and and_14 (and_14_out, not_7_out, not_8_out);
  and and_15 (and_15_out, not_9_out, H1);
  and and_16 (and_16_out, H1, not_10_out);
  and and_17 (and_17_out, and_4_out, H0);
  or or_6 (e, and_5_out, and_6_out);
  or or_7 (or_7_out, and_7_out, and_8_out);
  or or_8 (or_8_out, and_9_out, H3);
  or or_9 (or_9_out, and_10_out, and_11_out);
  or or_10 (or_10_out, and_12_out, H3);
  or or_11 (a, or_2_out, or_3_out);
  or or_12 (b, or_4_out, and_13_out);
  or or_13 (or_13_out, and_14_out, and_15_out);
  or or_14 (or_14_out, and_16_out, and_17_out);
  or or_15 (f, or_7_out, or_8_out);
  or or_16 (g, or_9_out, or_10_out);
  or or_17 (d, or_13_out, or_14_out);
endmodule

module Hours_tens (
  input  Htens,
  output a,
  output b,
  output c,
  output d,
  output e,
  output f,
  output g
);
endmodule
